# Fritzing sketch Automated Fire Extinguisher (saved by Fritzing 0.9.3b)
circuit board: 8.46667cm x 5.64444cm
breadboards: 1

parts:
  M1 = Keyes l9110 Fan module [package=THT]
  Mod1 = KY-026 Flame Sensor Module [package="Breakout board"]
  Part1 = Arduino Mega 2560 (Rev3)

nets:
  N1: M1.pin1, Part1.D7_PWM
  N2: M1.pin2, Part1.D8_PWM
  N3: M1.pin3, Mod1.G, Part1.GND
  N4: M1.pin4, Mod1.+, Part1.5V
  N5: Mod1.A0, Part1.A0

custom parts:
  Keyes l9110 Fan module: Keyes l9110 Fan module. Done from pictures without an actual board to hand so breadboard may not be fully accurate.
  KY-026 Flame Sensor Module: KY-026 Flame Sensor Module reacts in the presence of fire.

// code stored in the sketch: Untitled3.ino
int INA = 9; 
int INB = 8;
int flameSensorPin = A0;

int sensorReading;
void setup() 
{ 
  
  pinMode(INA,OUTPUT); 
  pinMode(INB,OUTPUT); 
  pinMode(flameSensorPin, OUTPUT);
  Serial.begin(9600);
  
}
 
void loop() 
{ 
  sensorReading = analogRead(flameSensorPin);
  Serial.println(sensorReading);
  

  if(sensorReading < 670){
    digitalWrite(INA,LOW);
    digitalWrite(INB,HIGH); 
   } else{
    digitalWrite(INA,LOW);
    digitalWrite(INB,LOW); 
    delay(1);
   
   }
  
}
